// Logisim project hw3_8.circ as structural Verilog: 3 circuits, main circuit hw3_8a
module hw3_8a (
  input  A,
  input  B,
  input  in_3,
  output D,
  output Borrow
);

  wire not_1_out;

  not not_1 (not_1_out, A);
  xor xor_1 (D, A, B);
  and and_1 (Borrow, not_1_out, B);
endmodule

module hw3_8b (
  input  A,
  input  B,
  input  C,
  output D,
  output Borrow
);

  wire and_1_out, and_2_out, and_3_out, not_1_out, xor_1_out;

  not not_1 (not_1_out, A);
  and and_1 (and_1_out, not_1_out, B);
  and and_2 (and_2_out, not_1_out, C);
  and and_3 (and_3_out, B, C);
  xor xor_1 (xor_1_out, A, B);
  xor xor_2 (D, xor_1_out, C);
  ExactlyOne xor_3 (.out(Borrow), .in0(and_1_out), .in1(and_2_out), .in2(and_3_out));
endmodule

module hw3_8c (
  input  x1,
  input  x2,
  input  x3,
  input  x4,
  input  y1,
  input  y2,
  input  y3,
  input  y4,
  output d1,
  output d2,
  output d3,
  output d4,
  output zero_result
);

  wire and_1_out, hw3_8b_1_borrow, hw3_8b_1_d, hw3_8b_2_borrow, hw3_8b_2_d, hw3_8b_3_borrow, hw3_8b_3_d,
       hw3_8b_4_borrow, hw3_8b_4_d, not_1_out, not_2_out, undriven;

  not not_1 (not_1_out, y4);
  and and_1 (and_1_out, y4, not_1_out);
  hw3_8b hw3_8b_1 (.A(x4), .B(y4), .C(and_1_out), .D(hw3_8b_1_d), .Borrow(hw3_8b_1_borrow));
  hw3_8b hw3_8b_2 (.A(x3), .B(y3), .C(hw3_8b_1_borrow), .D(hw3_8b_2_d), .Borrow(hw3_8b_2_borrow));
  hw3_8b hw3_8b_3 (.A(x2), .B(y2), .C(hw3_8b_2_borrow), .D(hw3_8b_3_d), .Borrow(hw3_8b_3_borrow));
  hw3_8b hw3_8b_4 (.A(x1), .B(y1), .C(hw3_8b_3_borrow), .D(hw3_8b_4_d), .Borrow(hw3_8b_4_borrow));
  not not_2 (not_2_out, undriven);
  buf and_2 (d1, not_2_out);  // AND_Gate
  and and_3 (d2, hw3_8b_3_borrow, not_2_out);
  buf and_4 (d3, not_2_out);  // AND_Gate
  and and_5 (d4, not_2_out, hw3_8b_1_borrow);
  nor nor_1 (zero_result, hw3_8b_1_d, hw3_8b_2_d, hw3_8b_3_d, hw3_8b_4_d);
endmodule
