// Logisim project hw3_9.circ as structural Verilog: 1 circuit, main circuit main
module main (
  input  x1,
  input  in_2,
  input  y0,
  input  y1,
  output x___0
);

  wire and_1_out, and_2_out, not_1_out, not_2_out;

  not not_1 (not_1_out, y0);
  and and_1 (and_1_out, in_2, x1, not_1_out, y1);
  not not_2 (not_2_out, y1);
  and and_2 (and_2_out, in_2, not_2_out);
  or or_1 (x___0, and_1_out, and_2_out);

  // Notes on the sheet:
  //   x0
endmodule
